// Logisim project ex1.circ as structural Verilog: 8 circuits, main circuit NAND1
module NAND1 (
  input  A,
  input  B,
  output RESULT
);

  wire and_1_out;

  and and_1 (and_1_out, A, B);
  not not_1 (RESULT, and_1_out);

  // Notes on the sheet:
  //   PUT CIRCUITRY HERE
endmodule

module NOR1 (
  input  A,
  input  B,
  output RESULT
);

  wire or_1_out;

  or or_1 (or_1_out, A, B);
  not not_1 (RESULT, or_1_out);

  // Notes on the sheet:
  //   PUT CIRCUITRY HERE
endmodule

module XOR1 (
  input  A,
  input  B,
  output RESULT
);

  wire and_1_out, and_2_out, not_1_out, not_2_out;

  not not_1 (not_1_out, A);
  not not_2 (not_2_out, B);
  and and_1 (and_1_out, not_1_out, B);
  and and_2 (and_2_out, A, not_2_out);
  or or_1 (RESULT, and_1_out, and_2_out);

  // Notes on the sheet:
  //   PUT CIRCUITRY HERE
endmodule

module MUX2 (
  input  A,
  input  B,
  input  Sel,
  output RESULT
);

  wire and_1_out, and_2_out, not_1_out;

  not not_1 (not_1_out, Sel);
  and and_1 (and_1_out, A, not_1_out);
  and and_2 (and_2_out, B, Sel);
  or or_1 (RESULT, and_1_out, and_2_out);

  // Notes on the sheet:
  //   PUT CIRCUITRY HERE
endmodule

module MUX4 (
  input  A,
  input  B,
  input  C,
  input  D,
  input  Sel1,
  input  Sel2,
  output RESULT
);

  wire and3_1_result, and3_2_result, and3_3_result, and3_4_result, not_1_out, not_2_out;

  not not_1 (not_1_out, Sel1);
  not not_2 (not_2_out, Sel2);
  AND3 and3_1 (.A(A), .B(not_1_out), .C(not_2_out), .RESULT(and3_1_result));
  AND3 and3_2 (.A(not_2_out), .B(Sel1), .C(B), .RESULT(and3_2_result));
  AND3 and3_3 (.A(not_1_out), .B(Sel2), .C(C), .RESULT(and3_3_result));
  AND3 and3_4 (.A(Sel1), .B(Sel2), .C(D), .RESULT(and3_4_result));
  OR4 or4_1 (.A(and3_1_result), .B(and3_2_result), .C(and3_3_result), .D(and3_4_result), .RESULT(RESULT));

  // Notes on the sheet:
  //   PUT CIRCUITRY HERE
endmodule

module AND3 (
  input  A,
  input  B,
  input  C,
  output RESULT
);

  wire and_1_out;

  and and_1 (and_1_out, A, B);
  and and_2 (RESULT, and_1_out, C);
endmodule

module OR3 (
  input  A,
  input  B,
  input  C,
  output RESULT
);

  wire or_1_out;

  or or_1 (or_1_out, A, B);
  or or_2 (RESULT, or_1_out, C);
endmodule

module OR4 (
  input  A,
  input  B,
  input  C,
  input  D,
  output RESULT
);

  wire or3_1_result;

  OR3 or3_1 (.A(A), .B(B), .C(C), .RESULT(or3_1_result));
  or or_1 (RESULT, or3_1_result, D);
endmodule
