// Logisim project csr.circ as structural Verilog: 1 circuit, main circuit csr
module csr (
  input  [11:0] CSR_address,
  input  [31:0] CSR_din,
  input  CSR_WE,
  input  clk,
  output [31:0] tohost
);

  wire and_1_out, and_2_out;

  and and_1 (and_1_out, ~CSR_address[0], CSR_address[1], CSR_address[2], CSR_address[3], CSR_address[4], ~CSR_address[5], ~CSR_address[6], ~CSR_address[7], CSR_address[8], ~CSR_address[9], CSR_address[10], ~CSR_address[11]);  // AND_Gate
  and and_2 (and_2_out, CSR_WE, and_1_out);
  Register #(.width(32)) register_1 (.D(CSR_din), .en(and_2_out), .clk(clk), .Q(tohost));  // open: clr

  // Other names for the same wires on the sheet: address[11:0] = CSR_address; data[31:0] = CSR_din; WE = CSR_WE

  // Notes on the sheet:
  //   INPUTS to your circuit
  //   DON'T CHANGE THE LOCATIONS OF THE INPUTS AND OUTPUTS!
  //   OUTPUT from your circuit
endmodule
