// Logisim project regfile.circ as structural Verilog: 1 circuit, main circuit regfile
module regfile (
  input  [4:0] rs1,
  input  [4:0] rs2,
  input  [4:0] rd,
  input  [31:0] Write_Data,
  input  RegWEn,
  input  clk,
  output [31:0] ra,
  output [31:0] sp,
  output [31:0] t0,
  output [31:0] t1,
  output [31:0] t2,
  output [31:0] s0,
  output [31:0] s1,
  output [31:0] a0,
  output [31:0] Read_Data_1,
  output [31:0] Read_Data_2
);

  wire x0write_en, x1write_en, x2write_en, x3write_en, x4write_en, x5write_en, x6write_en, x7write_en,
       x8write_en, x9write_en, x10write_en, x11write_en, x12write_en, x13write_en, x14write_en, x15write_en,
       x16write_en, x17write_en, x18write_en, x19write_en, x20write_en, x21write_en, x22write_en,
       x23write_en, x24write_en, x25write_en, x26write_en, x27write_en, x28write_en, x29write_en,
       x30write_en, x31write_en;
  wire [31:0] x0read_data1, x1read_data1, x2read_data1, x3read_data1, x4read_data1, x5read_data1,
       x6read_data1, x7read_data1, x8read_data1, x9read_data1, x10read_data1, x11read_data1, x12read_data1,
       x13read_data1, x14read_data1, x15read_data1, x16read_data1, x17read_data1, x18read_data1,
       x19read_data1, x20read_data1, x21read_data1, x22read_data1, x23read_data1, x24read_data1,
       x25read_data1, x26read_data1, x27read_data1, x28read_data1, x29read_data1, x30read_data1,
       x31read_data1;

  Demultiplexer #(.enable("false"), .select(5)) demultiplexer_1 (
    .out0(x0write_en), .out1(x1write_en), .out2(x2write_en), .out3(x3write_en), .out4(x4write_en),
    .out5(x5write_en), .out6(x6write_en), .out7(x7write_en), .out8(x8write_en), .out9(x9write_en),
    .out10(x10write_en), .out11(x11write_en), .out12(x12write_en), .out13(x13write_en), .out14(x14write_en),
    .out15(x15write_en), .out16(x16write_en), .out17(x17write_en), .out18(x18write_en), .out19(x19write_en),
    .out20(x20write_en), .out21(x21write_en), .out22(x22write_en), .out23(x23write_en), .out24(x24write_en),
    .out25(x25write_en), .out26(x26write_en), .out27(x27write_en), .out28(x28write_en), .out29(x29write_en),
    .out30(x30write_en), .out31(x31write_en), .in(RegWEn));  // open: sel
  Multiplexer #(.enable("false"), .select(5), .width(32)) multiplexer_1 (
    .in0(x0read_data1), .in1(x1read_data1), .in2(x2read_data1), .in3(x3read_data1), .in4(x4read_data1),
    .in5(x5read_data1), .in6(x6read_data1), .in7(x7read_data1), .in8(x8read_data1), .in9(x9read_data1),
    .in10(x10read_data1), .in11(x11read_data1), .in12(x12read_data1), .in13(x13read_data1),
    .in14(x14read_data1), .in15(x15read_data1), .in16(x16read_data1), .in17(x17read_data1),
    .in18(x18read_data1), .in19(x19read_data1), .in20(x20read_data1), .in21(x21read_data1),
    .in22(x22read_data1), .in23(x23read_data1), .in24(x24read_data1), .in25(x25read_data1),
    .in26(x26read_data1), .in27(x27read_data1), .in28(x28read_data1), .in29(x29read_data1),
    .in30(x30read_data1), .in31(x31read_data1), .out(Read_Data_1), .sel(rs1));
  Multiplexer #(.enable("false"), .select(5), .width(32)) multiplexer_2 (
    .in0(x0read_data1), .in1(x1read_data1), .in2(x2read_data1), .in3(x3read_data1), .in4(x4read_data1),
    .in5(x5read_data1), .in6(x6read_data1), .in7(x7read_data1), .in8(x8read_data1), .in9(x9read_data1),
    .in10(x10read_data1), .in11(x11read_data1), .in12(x12read_data1), .in13(x13read_data1),
    .in14(x14read_data1), .in15(x15read_data1), .in16(x16read_data1), .in17(x17read_data1),
    .in18(x18read_data1), .in19(x19read_data1), .in20(x20read_data1), .in21(x21read_data1),
    .in22(x22read_data1), .in23(x23read_data1), .in24(x24read_data1), .in25(x25read_data1),
    .in26(x26read_data1), .in27(x27read_data1), .in28(x28read_data1), .in29(x29read_data1),
    .in30(x30read_data1), .in31(x31read_data1), .out(Read_Data_2), .sel(rs2));
  Register #(.width(32)) x0 (.D(Write_Data), .en(x0write_en), .clk(clk), .Q(x0read_data1));  // open: clr
  Register #(.width(32)) x4 (.D(Write_Data), .en(x4write_en), .clk(clk), .Q(x4read_data1));  // open: clr
  Register #(.width(32)) x8 (.D(Write_Data), .en(x8write_en), .clk(clk), .Q(x8read_data1));  // open: clr
  Register #(.width(32)) x12 (.D(Write_Data), .en(x12write_en), .clk(clk), .Q(x12read_data1));  // open: clr
  Register #(.width(32)) x16 (.D(Write_Data), .en(x16write_en), .clk(clk), .Q(x16read_data1));  // open: clr
  Register #(.width(32)) x20 (.D(Write_Data), .en(x20write_en), .clk(clk), .Q(x20read_data1));  // open: clr
  Register #(.width(32)) x24 (.D(Write_Data), .en(x24write_en), .clk(clk), .Q(x24read_data1));  // open: clr
  Register #(.width(32)) x28 (.D(Write_Data), .en(x28write_en), .clk(clk), .Q(x28read_data1));  // open: clr
  Register #(.width(32)) x1 (.D(Write_Data), .en(x1write_en), .clk(clk), .Q(x1read_data1));  // open: clr
  Register #(.width(32)) x5 (.D(Write_Data), .en(x5write_en), .clk(clk), .Q(x5read_data1));  // open: clr
  Register #(.width(32)) x9 (.D(Write_Data), .en(x9write_en), .clk(clk), .Q(x9read_data1));  // open: clr
  Register #(.width(32)) x13 (.D(Write_Data), .en(x13write_en), .clk(clk), .Q(x13read_data1));  // open: clr
  Register #(.width(32)) x17 (.D(Write_Data), .en(x17write_en), .clk(clk), .Q(x17read_data1));  // open: clr
  Register #(.width(32)) x21 (.D(Write_Data), .en(x21write_en), .clk(clk), .Q(x21read_data1));  // open: clr
  Register #(.width(32)) x25 (.D(Write_Data), .en(x25write_en), .clk(clk), .Q(x25read_data1));  // open: clr
  Register #(.width(32)) x29 (.D(Write_Data), .en(x29write_en), .clk(clk), .Q(x29read_data1));  // open: clr
  Register #(.width(32)) x2 (.D(Write_Data), .en(x2write_en), .clk(clk), .Q(x2read_data1));  // open: clr
  Register #(.width(32)) x6 (.D(Write_Data), .en(x6write_en), .clk(clk), .Q(x6read_data1));  // open: clr
  Register #(.width(32)) x10 (.D(Write_Data), .en(x10write_en), .clk(clk), .Q(x10read_data1));  // open: clr
  Register #(.width(32)) x14 (.D(Write_Data), .en(x14write_en), .clk(clk), .Q(x14read_data1));  // open: clr
  Register #(.width(32)) x18 (.D(Write_Data), .en(x18write_en), .clk(clk), .Q(x18read_data1));  // open: clr
  Register #(.width(32)) x22 (.D(Write_Data), .en(x22write_en), .clk(clk), .Q(x22read_data1));  // open: clr
  Register #(.width(32)) x26 (.D(Write_Data), .en(x26write_en), .clk(clk), .Q(x26read_data1));  // open: clr
  Register #(.width(32)) x30 (.D(Write_Data), .en(x30write_en), .clk(clk), .Q(x30read_data1));  // open: clr
  Register #(.width(32)) x3 (.D(Write_Data), .en(x3write_en), .clk(clk), .Q(x3read_data1));  // open: clr
  Register #(.width(32)) x7 (.D(Write_Data), .en(x7write_en), .clk(clk), .Q(x7read_data1));  // open: clr
  Register #(.width(32)) x11 (.D(Write_Data), .en(x11write_en), .clk(clk), .Q(x11read_data1));  // open: clr
  Register #(.width(32)) x15 (.D(Write_Data), .en(x15write_en), .clk(clk), .Q(x15read_data1));  // open: clr
  Register #(.width(32)) x19 (.D(Write_Data), .en(x19write_en), .clk(clk), .Q(x19read_data1));  // open: clr
  Register #(.width(32)) x23 (.D(Write_Data), .en(x23write_en), .clk(clk), .Q(x23read_data1));  // open: clr
  Register #(.width(32)) x27 (.D(Write_Data), .en(x27write_en), .clk(clk), .Q(x27read_data1));  // open: clr
  Register #(.width(32)) x31 (.D(Write_Data), .en(x31write_en), .clk(clk), .Q(x31read_data1));  // open: clr

  // Other names for the same wires on the sheet: read_data1[31:0] = Read_Data_1; read_data2[31:0] = Read_Data_2;
  //   read_reg1[4:0] = rs1; read_reg2[4:0] = rs2; write_en = RegWEn; write_reg[4:0] = rd;
  //   x0read_data2[31:0] = x0read_data1; x1read_data2[31:0] = x1read_data1; x2read_data2[31:0] = x2read_data1;
  //   x3read_data2[31:0] = x3read_data1; x4read_data2[31:0] = x4read_data1; x5read_data2[31:0] = x5read_data1;
  //   x6read_data2[31:0] = x6read_data1; x7read_data2[31:0] = x7read_data1; x8read_data2[31:0] = x8read_data1;
  //   x9read_data2[31:0] = x9read_data1; x10read_data2[31:0] = x10read_data1; x11read_data2[31:0] = x11read_data1;
  //   x12read_data2[31:0] = x12read_data1; x13read_data2[31:0] = x13read_data1; x14read_data2[31:0] = x14read_data1;
  //   x15read_data2[31:0] = x15read_data1; x16read_data2[31:0] = x16read_data1; x17read_data2[31:0] = x17read_data1;
  //   x18read_data2[31:0] = x18read_data1; x19read_data2[31:0] = x19read_data1; x20read_data2[31:0] = x20read_data1;
  //   x21read_data2[31:0] = x21read_data1; x22read_data2[31:0] = x22read_data1; x23read_data2[31:0] = x23read_data1;
  //   x24read_data2[31:0] = x24read_data1; x25read_data2[31:0] = x25read_data1; x26read_data2[31:0] = x26read_data1;
  //   x27read_data2[31:0] = x27read_data1; x28read_data2[31:0] = x28read_data1; x29read_data2[31:0] = x29read_data1;
  //   x30read_data2[31:0] = x30read_data1; x31read_data2[31:0] = x31read_data1

  // Notes on the sheet:
  //   INPUTS to your circuit
  //   DON'T CHANGE THE LOCATIONS OF THE INPUTS AND OUTPUTS!
  //   These are DEBUG/TEST outputs from your circuit.
  //   OUTPUTS from your circuit
endmodule
